# Fritzing sketch NoCanDo (saved by Fritzing 0.9.3b)
breadboards: 1

parts:
  Part1 = Arduino Uno (Rev3)
  S1 = Pushbutton [package="[THT]"]
  R1 = Resistor [tolerance=±5% resistance=330 package=THT]
  3-Axis_Accelerometer1 = 3-Axis Accelerometer Breakout - MMA8452Q
  J1 = Basic Servo
  J2 = Basic Servo
  J3 = Basic Servo
  J4 = Piezo Speaker
  Lhi1 = LHi958 [package=to-39]
  R2 = Resistor [tolerance=±5% resistance=47k package="0603 [SMD]"]
  LED1 = LED - 3mm [color="Red (633nm)" package="3 mm [THT]"]
  R3 = Resistor [tolerance=±5% resistance=330 package="2512 [SMD]"]

nets:
  N1: Part1.A0, Lhi1.n.a., R2.Pin_0
  N2: Part1.D8, J4.pin2
  N3: Part1.D9_PWM, J3.pulse
  N4: Part1.D11_PWM/MOSI, J2.pulse
  N5: Part1.A4/SDA, 3-Axis_Accelerometer1.SDA
  N6: Part1.A5/SCL, 3-Axis_Accelerometer1.SCL
  VCC: Part1.D5_PWM, Part1.5V, S1.Pin_1, S1.Pin_2, R1.Pin_0, J1.vcc, J2.vcc, J3.vcc, Lhi1.D
  N7: Part1.D6_PWM, J1.pulse
  3V3: Part1.3V3, 3-Axis_Accelerometer1.3.3V
  GND: Part1.GND, R1.Pin_1, 3-Axis_Accelerometer1.GND, J1.gnd, J2.gnd, J3.gnd, Lhi1.GND, R2.Pin_1, R3.Pin_1
  N8: LED1.anode, R3.Pin_0
